// Logisim project hbcp.circ as structural Verilog: 5 circuits, main circuit dff
module dff (
  input  D,
  input  CLK,
  input  R,
  input  EN,
  output Q,
  output NOTQ
);

  wire multiplexer_1_out;

  Multiplexer multiplexer_1 (.in0(Q), .in1(D), .out(multiplexer_1_out), .sel(EN));
  D_Flip_Flop d_ff_1 (.D(multiplexer_1_out), .clk(CLK), .Q(Q), .Qn(NOTQ), .preset(1'b0), .reset(R));
endmodule

module main (
);

  wire ALUI, BRS, C, CALL, CLK, DECSP, FL, FWDA, FWDB, IMS, INCSP, J, LDI, N, nor_1_out, nor_2_out,
       not_1_out, not_2_out, PCS, RB, RR, RST, RW, SPS, STL, V, WEN, xor_1_out, xor_2_out, xor_3_out,
       xor_4_out, xor_5_out, xor_6_out, Z;
  wire [2:0] OS;
  wire [2:2] PCMUX;
  wire [7:0] adder_2_out, multiplexer_11_out, ram_1_p8, ram_1_p9, SPV, subtractor_1_out, undriven, undriven_2;
  wire [15:0] adder_1_out, ALUZ, and_1_out, bit_extender_1_out, bit_extender_2_out, bit_extender_3_out,
       bit_extender_4_out, DX, IMM, multiplexer_1_out, multiplexer_2_out, multiplexer_3_out,
       multiplexer_4_out, multiplexer_5_out, multiplexer_6_out, multiplexer_8_out, multiplexer_9_out,
       multiplexer_10_out, PCV, RA, registerfile_1_outb, RO, WB;

  Button button_1 (.out(RST));
  Clock clock_1 (.out(CLK));
  Adder #(.width(16)) adder_1 (.a(16'h2), .b(PCV), .out(adder_1_out), .cin(1'b0));  // open: cout
  not not_1 (not_1_out, RB);
  Multiplexer #(.width(16)) multiplexer_1 (.in0(DX), .in1(WB), .out(multiplexer_1_out));  // open: sel
  assign bit_extender_1_out = {{8{1'b0}}, SPV};  // Bit_Extender bit_extender_1
  Multiplexer #(.width(16)) multiplexer_2 (.in0(IMM), .in1(bit_extender_1_out), .out(multiplexer_2_out), .sel(SPS));
  Multiplexer #(.width(16)) multiplexer_3 (.in0(RA), .in1(PCV), .out(multiplexer_3_out), .sel(CALL));
  // RAM #(.addrWidth(16), .enables("line"), .line("dual")) ram_1: pin names not known; wires that end beside it: multiplexer_2_out, RW, 1'b1, not_1_out, CLK, multiplexer_3_out[7:0], multiplexer_3_out[15:8], ram_1_p8, ram_1_p9
  Multiplexer #(.select(3), .width(16)) multiplexer_4 (
    .in0(adder_1_out), .in1(adder_1_out), .in2(IMM), .in3(ALUZ), .in6(RO), .out(multiplexer_4_out),
    .sel({PCMUX[2], J, BRS}));  // open: in4, in5, in7
  registerfile registerfile_1 (
    .RSA(multiplexer_1_out[10:8]), .RSB(multiplexer_1_out[2:0]), .WE(WEN), .WS(WB[10:8]), .CLK(CLK),
    .RST(RST), .D(multiplexer_10_out), .OUTA(RA), .OUTB(registerfile_1_outb));
  Register #(.width(16)) register_1 (.D(multiplexer_4_out), .en(1'b1), .clk(CLK), .Q(PCV), .clr(RST));
  Multiplexer #(.width(16)) multiplexer_5 (.in0(RA), .in1(multiplexer_10_out), .out(multiplexer_5_out), .sel(FWDA));
  Multiplexer #(.width(16)) multiplexer_6 (
    .in0(registerfile_1_outb), .in1(multiplexer_10_out), .out(multiplexer_6_out), .sel(FWDB));
  assign bit_extender_2_out = {{8{1'b0}}, ram_1_p8};  // Bit_Extender bit_extender_2
  assign bit_extender_3_out = {{8{DX[7]}}, DX[7:0]};  // Bit_Extender bit_extender_3
  Multiplexer #(.width(16)) multiplexer_7 (.in0({ram_1_p9, ram_1_p8}), .in1(bit_extender_2_out), .out(RO), .sel(RB));
  Multiplexer #(.width(16)) multiplexer_8 (.in0(multiplexer_5_out), .in1(PCV), .out(multiplexer_8_out), .sel(PCS));
  Multiplexer #(.width(16)) multiplexer_9 (
    .in0(multiplexer_6_out), .in1(bit_extender_3_out), .out(multiplexer_9_out), .sel(IMS));
  // ROM #(.addrWidth(16), .line("dual")) rom_1: pin names not known; wires that end beside it: PCV
  Multiplexer #(.width(16)) multiplexer_10 (.in0(ALUZ), .in1(RO), .out(multiplexer_10_out), .sel(RR));
  alu alu_1 (
    .A(multiplexer_8_out), .B(multiplexer_9_out), .LOAD(ALUI), .CLK(CLK), .RST(RST), .RSTF(RST),
    .UFL(not_2_out), .OS(OS), .E(ALUZ), .N(N), .C(C), .Z(Z), .V(V));
  not not_2 (not_2_out, PCS);
  assign bit_extender_4_out = {{15{STL}}, STL};  // Bit_Extender bit_extender_4
  Register #(.width(16)) register_2 (.D({undriven_2, undriven}), .en(LDI), .clk(CLK), .Q(IMM), .clr(RST));
  assign and_1_out = bit_extender_4_out & {undriven_2, undriven};  // AND_Gate and_1, 16 bits wide
  Register #(.width(16)) register_3 (.D(and_1_out), .en(1'b1), .clk(CLK), .Q(DX), .clr(FL));
  control control_1 (
    .DX(DX), .N(N), .Z(Z), .C(C), .V(V), .WB(WB), .WEN(WEN), .SPS(SPS), .RET(PCMUX[2]), .J(J), .CALL(CALL),
    .BRS(BRS), .RW(RW), .RR(RR), .RBYTE(RB), .FLUSH(FL), .INCSP(INCSP), .DECSP(DECSP), .OS(OS), .IMS(IMS),
    .ALUI(ALUI), .STALL(STL), .LDI(LDI), .PCS(PCS));
  Multiplexer #(.select(2), .width(8)) multiplexer_11 (
    .in0(SPV), .in1(adder_2_out), .in2(subtractor_1_out), .in3(SPV), .out(multiplexer_11_out),
    .sel({DECSP, INCSP}));
  Register register_4 (.D(multiplexer_11_out), .en(1'b1), .clk(CLK), .Q(SPV), .clr(RST));
  Register #(.width(16)) register_5 (.D(DX), .en(1'b1), .clk(CLK), .Q(WB), .clr(RST));
  xor xor_1 (xor_1_out, DX[10], WB[10]);
  xor xor_2 (xor_2_out, DX[9], WB[9]);
  xor xor_3 (xor_3_out, DX[8], WB[8]);
  xor xor_4 (xor_4_out, DX[2], WB[10]);
  xor xor_5 (xor_5_out, DX[1], WB[9]);
  xor xor_6 (xor_6_out, DX[0], WB[8]);
  nor nor_1 (nor_1_out, xor_1_out, xor_2_out, xor_3_out);
  nor nor_2 (nor_2_out, xor_4_out, xor_5_out, xor_6_out);
  Register #(.width(16)) register_6 (.D(WB), .en(1'b1), .clk(CLK), .clr(RST));  // open: Q
  Adder adder_2 (.a(SPV), .b(8'h2), .out(adder_2_out), .cin(1'b0));  // open: cout
  Subtractor subtractor_1 (.a(SPV), .b(8'h2), .out(subtractor_1_out), .bin(1'b0));  // open: bout
  and and_2 (FWDA, nor_1_out, WEN);
  and and_3 (FWDB, WEN, nor_2_out);

  // Other names for the same wires on the sheet: PCMUX[1:0] = {J, BRS}; RET = PCMUX[2]

  // Notes on the sheet:
  //   Register File + ALU
  //   RAM + Stack
  //   contents of rom_1 (hex, n*v repeats v):
  //   8 0 9 ff e8 0 5 0 31 0 40 f8 38 fe 1266*0 10 1 e8 0 6 0 f0 249*0 19 1 f0
  //   Stack Pointer
  //   Forwarding Logic
endmodule

module registerfile (
  input  [15:0] D,
  input  WE,
  input  [2:0] RSA,
  input  [2:0] WS,
  input  [2:0] RSB,
  input  CLK,
  input  RST,
  output [15:0] OUTA,
  output [15:0] OUTB
);

  wire demultiplexer_1_out0, demultiplexer_1_out1, demultiplexer_1_out2, demultiplexer_1_out3,
       demultiplexer_1_out4, demultiplexer_1_out5, demultiplexer_1_out6, demultiplexer_1_out7;
  wire [15:0] register_1_q, register_2_q, register_3_q, register_4_q, register_5_q, register_6_q,
       register_7_q, register_8_q;

  Demultiplexer #(.select(3)) demultiplexer_1 (
    .out0(demultiplexer_1_out0), .out1(demultiplexer_1_out1), .out2(demultiplexer_1_out2),
    .out3(demultiplexer_1_out3), .out4(demultiplexer_1_out4), .out5(demultiplexer_1_out5),
    .out6(demultiplexer_1_out6), .out7(demultiplexer_1_out7), .in(WE), .sel(WS));
  Register #(.width(16)) register_1 (.D(D), .en(demultiplexer_1_out0), .clk(CLK), .Q(register_1_q), .clr(RST));
  Register #(.width(16)) register_2 (.D(D), .en(demultiplexer_1_out1), .clk(CLK), .Q(register_2_q), .clr(RST));
  Register #(.width(16)) register_3 (.D(D), .en(demultiplexer_1_out2), .clk(CLK), .Q(register_3_q), .clr(RST));
  Register #(.width(16)) register_4 (.D(D), .en(demultiplexer_1_out3), .clk(CLK), .Q(register_4_q), .clr(RST));
  Register #(.width(16)) register_5 (.D(D), .en(demultiplexer_1_out4), .clk(CLK), .Q(register_5_q), .clr(RST));
  Register #(.width(16)) register_6 (.D(D), .en(demultiplexer_1_out5), .clk(CLK), .Q(register_6_q), .clr(RST));
  Register #(.width(16)) register_7 (.D(D), .en(demultiplexer_1_out6), .clk(CLK), .Q(register_7_q), .clr(RST));
  Register #(.width(16)) register_8 (.D(D), .en(demultiplexer_1_out7), .clk(CLK), .Q(register_8_q), .clr(RST));
  Multiplexer #(.select(3), .width(16)) multiplexer_1 (
    .in0(register_1_q), .in1(register_2_q), .in2(register_3_q), .in3(register_4_q), .in4(register_5_q),
    .in5(register_6_q), .in6(register_7_q), .in7(register_8_q), .out(OUTA), .sel(RSA));
  Multiplexer #(.select(3), .width(16)) multiplexer_2 (
    .in0(register_1_q), .in1(register_2_q), .in2(register_3_q), .in3(register_4_q), .in4(register_5_q),
    .in5(register_6_q), .in6(register_7_q), .in7(register_8_q), .out(OUTB), .sel(RSB));
endmodule

module alu (
  input  [15:0] A,
  input  [15:0] B,
  input  LOAD,
  input  CLK,
  input  RST,
  input  [2:0] OS,
  input  RSTF,
  input  UFL,
  output [15:0] E,
  output N,
  output Z,
  output C,
  output V
);

  wire and_2_out, and_3_out, and_4_out, and_5_out, CLKn, COUT, multiplexer_2_out, nor_1_out, or_3_out, UF,
       VOUT;
  wire [2:0] OSL;
  wire [7:0] register_4_q;
  wire [15:0] adder_1_out, and_1_out, bit_extender_1_out, bit_extender_2_out, or_1_out, register_3_q,
       xor_1_out;
  wire [15:8] register_4_q_2;

  not not_1 (CLKn, CLK);
  Register #(.width(1)) register_1 (.D(UFL), .en(LOAD), .clk(CLK), .Q(UF), .clr(RST));
  Register #(.width(3)) register_2 (.D(OS), .en(LOAD), .clk(CLK), .Q(OSL), .clr(RST));
  Register #(.width(16)) register_3 (.D(A), .en(LOAD), .clk(CLK), .Q(register_3_q), .clr(RST));
  Register #(.width(16)) register_4 (.D(B), .en(LOAD), .clk(CLK), .Q({register_4_q_2, register_4_q}), .clr(RST));
  assign bit_extender_1_out = {{15{OSL[2]}}, OSL[2]};  // Bit_Extender bit_extender_1
  assign xor_1_out = bit_extender_1_out ^ {register_4_q_2, register_4_q};  // XOR_Gate xor_1, 16 bits wide
  assign and_1_out = register_3_q & {register_4_q_2, register_4_q};  // AND_Gate and_1, 16 bits wide
  assign or_1_out = register_3_q | {register_4_q_2, register_4_q};  // OR_Gate or_1, 16 bits wide
  Adder #(.width(16)) adder_1 (.a(register_3_q), .b(xor_1_out), .out(adder_1_out), .cin(OSL[0]), .cout(COUT));
  and and_2 (and_2_out, ~E[15], register_3_q[15], xor_1_out[15]);  // AND_Gate
  and and_3 (and_3_out, E[15], ~register_3_q[15], ~xor_1_out[15]);  // AND_Gate
  or or_2 (VOUT, and_2_out, and_3_out);
  assign bit_extender_2_out = {{8{1'b0}}, register_4_q};  // Bit_Extender bit_extender_2
  and and_4 (and_4_out, ~OSL[0], ~OSL[1], ~OSL[2]);  // AND_Gate
  and and_5 (and_5_out, OSL[0], ~OSL[1], OSL[2]);  // AND_Gate
  Multiplexer #(.select(3), .width(16)) multiplexer_1 (
    .in0(adder_1_out), .in1(and_1_out), .in2(or_1_out), .in3(bit_extender_2_out), .in4(xor_1_out),
    .in5(adder_1_out), .out(E), .sel(OSL));  // open: in6, in7
  or or_3 (or_3_out, and_4_out, and_5_out);
  Multiplexer multiplexer_2 (.in0(1'b0), .in1(UF), .out(multiplexer_2_out));  // open: sel
  Register #(.width(1)) register_5 (.D(E[15]), .en(UF), .clk(CLKn), .Q(N), .clr(RSTF));
  Register #(.width(1)) register_6 (.D(COUT), .en(multiplexer_2_out), .clk(CLKn), .Q(C), .clr(RSTF));
  nor nor_1 (nor_1_out, E[15], E[14], E[13], E[12], E[11], E[10], E[9], E[8], E[7], E[6], E[5], E[4], E[3], E[2], E[1], E[0]);
  Register #(.width(1)) register_7 (.D(nor_1_out), .en(UF), .clk(CLKn), .Q(Z), .clr(RSTF));
  Register #(.width(1)) register_8 (.D(VOUT), .en(multiplexer_2_out), .clk(CLKn), .Q(V), .clr(RSTF));
endmodule

module control (
  input  [15:0] WB,
  input  [15:0] DX,
  input  N,
  input  Z,
  input  C,
  input  V,
  output J,
  output RW,
  output RBYTE,
  output IMS,
  output PCS,
  output INCSP,
  output WEN,
  output BRS,
  output RR,
  output [2:0] OS,
  output ALUI,
  output LDI,
  output FLUSH,
  output STALL,
  output RET,
  output DECSP,
  output SPS,
  output CALL
);

  wire [5:5] rom_2_data;
  wire [7:1] rom_1_data;
  wire [7:3] rom_4_data;

  ROM rom_1 (.addr(DX[15:8]), .data({rom_1_data, DECSP}));
  ROM rom_2 (.addr(DX[15:8]), .data({PCS, LDI, rom_2_data[5], ALUI, IMS, OS}));
  not not_1 (STALL, rom_2_data[5]);
  ROM #(.addrWidth(12)) rom_3 (.addr({N, Z, C, V, WB[15:8]}), .data({INCSP, FLUSH, RBYTE, RR, RW, BRS, J, WEN}));
  ROM #(.addrWidth(12)) rom_4 (.addr({N, Z, C, V, WB[15:8]}), .data({rom_4_data, CALL, RET, SPS}));

  // Notes on the sheet:
  //   contents of rom_1 (hex, n*v repeats v):
  //   224*0 8*1 8*0 8*1
  //   contents of rom_2 (hex, n*v repeats v):
  //   8*0 8*1b 8*18 8*1d 8*19 8*1a 8*1d 8*b8 64*98 8*13 8*10 8*15 8*11 8*12 8*14 8*15 32*60 16*0 8*60 8*0
  //   8*60
  //   contents of rom_3 (hex, n*v repeats v):
  //   8*0 40*1 8*0 8*6 8*46 16*4 16*46 16*4 8*46 48*1 8*0 8*11 8*31 8*8 8*28 8*88 8*11 8*ca 8*52 8*2 8*0
  //   40*1 8*0 8*6 8*46 16*4 8*46 8*4 16*46 8*4 48*1 8*0 8*11 8*31 8*8 8*28 8*88 8*11 8*ca 8*52 8*2 8*0
  //   40*1 8*0 8*6 8*46 8*4 8*46 8*4 8*46 16*4 8*46 48*1 8*0 8*11 8*31 8*8 8*28 8*88 8*11 8*ca 8*52 8*2
  //   8*0 40*1 8*0 8*6 8*46 8*4 8*46 16*4 16*46 8*4 48*1 8*0 8*11 8*31 8*8 8*28 8*88 8*11 8*ca 8*52 8*2
  //   8*0 40*1 8*0 8*6 8*4 8*46 8*4 16*46 16*4 8*46 48*1 8*0 8*11 8*31 8*8 8*28 8*88 8*11 8*ca 8*52 8*2
  //   8*0 40*1 8*0 8*6 8*4 8*46 8*4 32*46 8*4 48*1 8*0 8*11 8*31 8*8 8*28 8*88 8*11 8*ca 8*52 8*2 8*0 40*1
  //   8*0 8*6 8*4 16*46 8*4 8*46 16*4 8*46 48*1 8*0 8*11 8*31 8*8 8*28 8*88 8*11 8*ca 8*52 8*2 8*0 40*1
  //   8*0 8*6 8*4 16*46 8*4 24*46 8*4 48*1 8*0 8*11 8*31 8*8 8*28 8*88 8*11 8*ca 8*52 8*2 8*0 40*1 8*0 8*6
  //   8*46 16*4 8*46 8*4 8*46 8*4 8*46 48*1 8*0 8*11 8*31 8*8 8*28 8*88 8*11 8*ca 8*52 8*2 8*0 40*1 8*0
  //   8*6 8*46 16*4 16*46 8*4 8*46 8*4 48*1 8*0 8*11 8*31 8*8 8*28 8*88 8*11 8*ca 8*52 8*2 8*0 40*1 8*0
  //   8*6 8*46 8*4 8*46 16*4 8*46 8*4 8*46 48*1 8*0 8*11 8*31 8*8 8*28 8*88 8*11 8*ca 8*52 8*2 8*0 40*1
  //   8*0 8*6 8*46 8*4 8*46 8*4 8*46 8*4 8*46 8*4 48*1 8*0 8*11 8*31 8*8 8*28 8*88 8*11 8*ca 8*52 8*2 8*0
  //   40*1 8*0 8*6 8*4 8*46 8*4 24*46 8*4 8*46 48*1 8*0 8*11 8*31 8*8 8*28 8*88 8*11 8*ca 8*52 8*2 8*0
  //   40*1 8*0 8*6 8*4 8*46 8*4 16*46 8*4 8*46 8*4 48*1 8*0 8*11 8*31 8*8 8*28 8*88 8*11 8*ca 8*52 8*2 8*0
  //   40*1 8*0 8*6 8*4 16*46 8*4 16*46 8*4 8*46 48*1 8*0 8*11 8*31 8*8 8*28 8*88 8*11 8*ca 8*52 8*2 8*0
  //   40*1 8*0 8*6 8*4 16*46 8*4 8*46 8*4 8*46 8*4 48*1 8*0 8*11 8*31 8*8 8*28 8*88 8*11 8*ca 8*52 8*2
  //   contents of rom_4 (hex, n*v repeats v):
  //   216*0 16*1 8*5 8*3 224*0 16*1 8*5 8*3 224*0 16*1 8*5 8*3 224*0 16*1 8*5 8*3 224*0 16*1 8*5 8*3 224*0
  //   16*1 8*5 8*3 224*0 16*1 8*5 8*3 224*0 16*1 8*5 8*3 224*0 16*1 8*5 8*3 224*0 16*1 8*5 8*3 224*0 16*1
  //   8*5 8*3 224*0 16*1 8*5 8*3 224*0 16*1 8*5 8*3 224*0 16*1 8*5 8*3 224*0 16*1 8*5 8*3 224*0 16*1 8*5
  //   8*3
endmodule
